# Fritzing sketch artifactory_draw_circuit (saved by Fritzing 0.9.3b)
breadboards: 1

parts:
  WeMos_D1_Mini1 = WeMos D1 Mini
  S1 = SWITCH-MOMENTARY-2 [package=tactile-pth-12mm]
  5V_Supply = Power plug
  IC1 = IC, DIP package, 20 pins [chip_label=74HC245N]
  Plug_to_LED_Matrix = Header 3 [package=1x03-1mm-ra]
  R1 = Resistor [tolerance=±5% resistance=470 package=THT]
  C1 = Electrolytic Capacitor [capacitance=100µF voltage=16V part_number=1000µF package="200 mil [THT, electrolytic]"]

nets:
  5V: WeMos_D1_Mini1.5V, 5V_Supply.VCC, Plug_to_LED_Matrix.1, C1.+
  N1: WeMos_D1_Mini1.D1, IC1.pin18
  N2: WeMos_D1_Mini1.D2, S1.1
  N3: WeMos_D1_Mini1.G, S1.2, 5V_Supply.GND, IC1.pin1, IC1.pin10, IC1.pin19, Plug_to_LED_Matrix.3, C1.-
  N4: IC1.pin2, R1.Pin_1
  N5: Plug_to_LED_Matrix.2, R1.Pin_0
